// Digital circuit IR.dig as structural Verilog
module IR (
  input  [3:0] Input,
  input  [1:0] CTRL__Load__Store,
  input  clk,
  output [3:0] Output
);

  _4_bit_register _4_bit_register_1 (
    .Input(Input), .CTRL__Load__Store__Clear(CTRL__Load__Store), .clk(clk), .Output(Output));
endmodule
