// Digital circuit 4-bit-processor.dig as structural Verilog
module _4_bit_processor (
  input  clk,
  input  [1:0] IR_ctrl,
  input  [3:0] Mem_input,
  input  [1:0] Mem_ctrl,
  input  [1:0] pc_ctrl,
  output [15:0] Instructions_16_bit,
  output [3:0] PC_Output,
  output [3:0] ALU_out,
  output [3:0] data_1_out,
  output [3:0] data_2_out
);

  wire [7:0] registerfile_write_ctrl_1_write_ctrl;

  intr_mem_module intr_mem_module_1 (
    .clk(clk), .IR_ctrl(IR_ctrl), .pc_ctrl(pc_ctrl), .instr_mem_input(Mem_input), .intr_mem_ctrl(Mem_ctrl),
    .pc_output(PC_Output), .ir_output(Instructions_16_bit));
  RegisterFile_Write_ctrl registerfile_write_ctrl_1 (
    .OpCode3(Instructions_16_bit[1:0]), .write_ctrl(registerfile_write_ctrl_1_write_ctrl));
  Register_file register_file_1 (
    .clk(clk), .Write_data(ALU_out), .Select_write(Instructions_16_bit[1:0]),
    .ctrl_registers(registerfile_write_ctrl_1_write_ctrl), .Select_read1(Instructions_16_bit[5:4]),
    .Select_read2(Instructions_16_bit[3:2]), .Read_data_1(data_1_out), .Read_data_2(data_2_out));
  ALU alu_1 (.S_1_S_0_C_in(Instructions_16_bit[8:6]), .B(data_2_out), .A(data_1_out), .D(ALU_out));  // open: Overflow
endmodule

/* Test case Test-circuit:
IR-ctrl Mem-ctrl Mem-input pc-ctrl clk PC-Output Instructions-16-bit ALU-out data-1-out data-2-out
0 1 1 1 c x x x x x
0 1 2 1 c x x x x x
0 1 3 1 c x x x x x
0 1 4 1 c x x x x x
0 1 5 1 c x x x x x
0 1 6 1 c x x x x x
0 1 7 1 c x x x x x
1 0 0 1 c x x x x x
1 0 0 1 c x x x x x
1 0 0 1 c x x x x x
1 0 0 1 c x x x x x
1 0 0 1 c x x x x x
1 0 0 1 c x x x x x
1 0 0 1 c x x x x x
1 0 0 1 c x x x x x
1 0 0 1 c x x x x x
*/
